# Fritzing sketch switch led Sketch (saved by Fritzing 0.9.2b)
circuit board: 8.46667cm x 5.64444cm
breadboards: 1

parts:
  R2 = Resistor [tolerance=±5% resistance=10k package=THT]
  Part2 = Arduino Uno (Rev3)
  S1 = Pushbutton [package="[THT]"]
  LED1 = LED - 5mm [color="Red (633nm)" package="5 mm [THT]"]
  R3 = Resistor [tolerance=±5% resistance=330k package=THT]

nets:
  N1: R2.Pin_0, Part2.D12/MISO, S1.Pin_1, S1.Pin_2
  N2: R2.Pin_1, Part2.GND, R3.Pin_1
  N3: Part2.D2, LED1.cathode
  N4: Part2.5V, S1.Pin_3, S1.Pin_4
  N5: LED1.anode, R3.Pin_0
